# Fritzing sketch Ejection System (saved by Fritzing 0.9.5d)

parts:
  ESP32-C3_Super_Mini = Esp32-c3 super mini
  GY-BME-280 = BME280
  MG996R_Servo = Basic Servo
  5v_3A_BEC_Converter = Mini-360 DC-DC Buck converter [package=THT]
  2s_7_4v_350MaH_LiPo_Battery = 2.1mm Barrel Jack with Terminal Block

nets:
  N1: ESP32-C3_Super_Mini.Pin_9, GY-BME-280.SCL
  N2: ESP32-C3_Super_Mini.Pin_10, GY-BME-280.SDA
  N3: ESP32-C3_Super_Mini.Pin_12, MG996R_Servo.pulse
  N4: ESP32-C3_Super_Mini.Pin_14, GY-BME-280.VIN
  GND: ESP32-C3_Super_Mini.Pin_15, GY-BME-280.GND, MG996R_Servo.gnd, 5v_3A_BEC_Converter.IN-
  N5: ESP32-C3_Super_Mini.Pin_16, MG996R_Servo.vcc, 5v_3A_BEC_Converter.IN+
  N6: 5v_3A_BEC_Converter.OUT+, 2s_7_4v_350MaH_LiPo_Battery.POS
  N7: 5v_3A_BEC_Converter.OUT-, 2s_7_4v_350MaH_LiPo_Battery.NEG

custom parts:
  Esp32-c3 super mini: ESP32-C3 Development Board ESP32 SuperMini Development Board ESP32 Development Board WiFi Bluetooth.
  BME280: Temperature Humidity Barometric presure Sensor
  Mini-360 DC-DC Buck converter: Mini-360 DC-DC Buck converter. Tiny buck step down voltage converter, input voltage 4.75 to 23V output 1 to 17V adjustable. Available from ebay and the like.
