# Fritzing sketch Igniter (saved by Fritzing 0.9.5d)

parts:
  ESP32_v1_DevKit = DOIT Esp32 DevKit v1 (30 pins long, 11 pins width) [part_number=ESP32S-PIN30]
  9v_Battery = Battery block 9V
  1_Channel_5v_Relay_Module = 1 chan 5v relay module
  Buzzer = Piezo Speaker
  Nichrome_Wire = Resistor [tolerance=±5% resistance=1 package="2010 [SMD]"]

nets:
  N1: ESP32_v1_DevKit.GND, 1_Channel_5v_Relay_Module.pin_2, Buzzer.pin1
  N2: ESP32_v1_DevKit.TX2, Buzzer.pin2
  N3: ESP32_v1_DevKit.D26, 1_Channel_5v_Relay_Module.pin_3
  N4: ESP32_v1_DevKit.VIN, 1_Channel_5v_Relay_Module.pin_1
  N5: 9v_Battery.-, Nichrome_Wire.Pin_0
  N6: 9v_Battery.+, 1_Channel_5v_Relay_Module.pin_5
  N7: 1_Channel_5v_Relay_Module.pin_4, Nichrome_Wire.Pin_1

custom parts:
  DOIT Esp32 DevKit v1 (30 pins long, 11 pins width): The DOIT Esp32 DevKit v1 is one of the development board created by DOIT to evaluate the ESP-WROOM-32 module. It is based on the ESP32 microcontroller that boasts Wifi, Bluetooth, Ethernet and Low Power support all in a single chip. (vanepp) made breadboard work, adjusted pin numbering and labels and reduced size of schematic and cleaned up pcb. This chip is 30pins long (2 x15) and 11 pins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
  1 chan 5v relay module: 1 Channel 5V Relay Module Board Shield with Optocoupler Support High and Low Level Trigger for Arduino.
